// Logisim project 220323_halfAdder.circ as structural Verilog: 1 circuit, main circuit main
module main (
  input  A,
  input  B,
  output C,
  output S
);

  and and_1 (C, A, B);
  xor xor_1 (S, A, B);

  // Notes on the sheet:
  //   19101279 조계진
  //   Truth Table
  //   A  B  |  C  S
  //   0  0  |  0  0
  //   0  1  |  0  1
  //   1  0  |  0  1
  //   1  1  |  1  0
endmodule
