// Logisim project 230402_7segment.circ as structural Verilog: 1 circuit, main circuit main
module main (
  input  B0,
  input  B1,
  input  B2,
  input  B3
);

  wire [6:0] Controller_p2;

  // PlaRom #(.Contents("0 0 2 0 2 0*4 2 0 2 0 1 0 1 2 0*4 1 0*4 2 2 0 0 1 1 0 2 0 0 2 0*5 1 0*4 2 0 0 2 1 0 2 1 2 0 1 0 1 0 1 2 0*3 2 1 0 1 0 1 2 0*5 1 1 0 2 1 0 0 2 0 1 2 0*5 2 1 0 2 1 0 0 1 2 0 1 0*6 1 0*6 1 0*6 1 0*7 1 0*6 1 0*6 1 0*6 1 0*7 1 0*6 1 0*6 1 0*6 1 0*7 1 0*6 1 0*6 1 0*6 1 0*7 1 0*6 1 0*7 1 0*6 1 0*6 1 0*6 1 0*7 1 0*6 1 0*6 1 0*6 1"), .\and (26), .outputs(7)) Controller: pin names not known; wires that end beside it: {B0, B1, B2, B3}, Controller_p2
  _7_Segment_Display u_7_segment_display_1 (
    .g(Controller_p2[0]), .f(Controller_p2[1]), .a(Controller_p2[6]), .b(Controller_p2[5]),
    .e(Controller_p2[2]), .d(Controller_p2[3]), .c(Controller_p2[4]));  // open: dp
endmodule
