// Logisim project 230402_fullAdder_PLA.circ as structural Verilog: 1 circuit, main circuit main
module main (
  input  A,
  input  B,
  input  C
);

  wire [1:0] FullAdder_p2;

  // PlaRom #(.Contents("1 2*3 1 2*3 1 2*3 1 1 2 1 2 1 2 1 1 2*3 1 0 1 0 1 0 1 0 0 1 0 1 0 1 0 1"), .\and (8), .outputs(2)) FullAdder: pin names not known; wires that end beside it: {C, B, A}, FullAdder_p2
  LED C_out (.in(FullAdder_p2[1]));
  LED S (.in(FullAdder_p2[0]));
endmodule
