// Logisim project 230402_fullAdder_ROM.circ as structural Verilog: 1 circuit, main circuit main
module main (
  input  A,
  input  B,
  input  C
);

  wire [1:0] FullAdder_out;

  PLA #(.in_width(3), .\table ("000 00\n001 01\n010 01\n011 10\n100 01\n101 10\n110 10\n111 11")) FullAdder (
    .in({C, B, A}), .out(FullAdder_out));
  LED C_out (.in(FullAdder_out[1]));
  LED S (.in(FullAdder_out[0]));
endmodule
