// Logisim project 230406_8bitRippleCarryAdder.circ as structural Verilog: 3 circuits, main circuit main
module main (
  input  [7:0] A,
  input  [7:0] B,
  input  SUBTRACT,
  output [7:0] S,
  output OVERFLOW
);

  wire fulladder_1_c_out, fulladder_2_c_out, fulladder_3_c_out, fulladder_4_c_out, fulladder_5_c_out,
       fulladder_6_c_out, fulladder_7_c_out, xor_1_out, xor_2_out, xor_3_out, xor_4_out, xor_5_out,
       xor_6_out, xor_7_out, xor_8_out;

  xor xor_1 (xor_1_out, B[0], SUBTRACT);
  xor xor_2 (xor_2_out, B[1], SUBTRACT);
  xor xor_3 (xor_3_out, B[2], SUBTRACT);
  xor xor_4 (xor_4_out, B[3], SUBTRACT);
  xor xor_5 (xor_5_out, B[4], SUBTRACT);
  xor xor_6 (xor_6_out, B[5], SUBTRACT);
  xor xor_7 (xor_7_out, B[6], SUBTRACT);
  xor xor_8 (xor_8_out, B[7], SUBTRACT);
  fullAdder fulladder_1 (.A(A[0]), .B(xor_1_out), .C(SUBTRACT), .S(S[0]), .C_out(fulladder_1_c_out));
  fullAdder fulladder_2 (.A(A[1]), .B(xor_2_out), .C(fulladder_1_c_out), .S(S[1]), .C_out(fulladder_2_c_out));
  fullAdder fulladder_3 (.A(A[2]), .B(xor_3_out), .C(fulladder_2_c_out), .S(S[2]), .C_out(fulladder_3_c_out));
  fullAdder fulladder_4 (.A(A[3]), .B(xor_4_out), .C(fulladder_3_c_out), .S(S[3]), .C_out(fulladder_4_c_out));
  fullAdder fulladder_5 (.A(A[4]), .B(xor_5_out), .C(fulladder_4_c_out), .S(S[4]), .C_out(fulladder_5_c_out));
  fullAdder fulladder_6 (.A(A[5]), .B(xor_6_out), .C(fulladder_5_c_out), .S(S[5]), .C_out(fulladder_6_c_out));
  fullAdder fulladder_7 (.A(A[6]), .B(xor_7_out), .C(fulladder_6_c_out), .S(S[6]), .C_out(fulladder_7_c_out));
  fullAdder fulladder_8 (.A(A[7]), .B(xor_8_out), .C(fulladder_7_c_out), .S(S[7]), .C_out(OVERFLOW));

  // Other names for the same wires on the sheet: SUB = SUBTRACT
endmodule

module halfAdder (
  input  A,
  input  B,
  output S,
  output C
);

  xor xor_1 (S, A, B);
  and and_1 (C, A, B);
endmodule

module fullAdder (
  input  A,
  input  B,
  input  C,
  output S,
  output C_out
);

  wire halfadder_1_c, halfadder_1_s, halfadder_2_c;

  halfAdder halfadder_1 (.A(A), .B(B), .S(halfadder_1_s), .C(halfadder_1_c));
  halfAdder halfadder_2 (.A(halfadder_1_s), .B(C), .S(S), .C(halfadder_2_c));
  or or_1 (C_out, halfadder_1_c, halfadder_2_c);
endmodule
