// Logisim project 230420_latchAndFlipFlop.circ as structural Verilog: 1 circuit, main circuit main
module main (
  input  R,
  input  S,
  input  in_3,
  input  in_4,
  input  in_5,
  output out_6,
  output out_7,
  output out_8,
  output out_9
);

  wire clock_1_out;

  Clock clock_1 (.out(clock_1_out));
  J_K_Flip_Flop j_k_ff_1 (.J(in_4), .K(in_5), .clk(clock_1_out), .Q(out_9));  // open: Qn, preset, reset
  not nor_1 (out_6, out_7);  // NOR_Gate
  nor nor_2 (out_7, out_6, S);
  // Buffer buffer_1 has open pins: in=open, out=out_8
endmodule
