// Logisim project 230427_8bitSynchronousCounter.circ as structural Verilog: 2 circuits, main circuit main
module main (
  input  in_1
);

  wire clock_1_out;
  wire [7:0] counter8_1_count;

  Clock clock_1 (.out(clock_1_out));
  Hex_Digit_Display hex_digit_display_1 (.value(counter8_1_count[7:4]));  // open: dp
  Counter8 counter8_1 (.ENABLE(in_1), .CLK(clock_1_out), .COUNT(counter8_1_count));
  Hex_Digit_Display hex_digit_display_2 (.value(counter8_1_count[3:0]));  // open: dp
endmodule

module Counter8 (
  input  ENABLE,
  input  CLK,
  output [7:0] COUNT
);

  wire and_1_out, and_2_out, and_3_out, and_4_out, and_5_out, and_6_out, and_7_out;

  J_K_Flip_Flop j_k_ff_1 (.J(ENABLE), .K(ENABLE), .clk(CLK), .Q(COUNT[0]));  // open: Qn, preset, reset
  and and_1 (and_1_out, ENABLE, COUNT[0]);
  J_K_Flip_Flop j_k_ff_2 (.J(and_1_out), .K(and_1_out), .clk(CLK), .Q(COUNT[1]));  // open: Qn, preset, reset
  and and_2 (and_2_out, and_1_out, COUNT[1]);
  J_K_Flip_Flop j_k_ff_3 (.J(and_2_out), .K(and_2_out), .clk(CLK), .Q(COUNT[2]));  // open: Qn, preset, reset
  and and_3 (and_3_out, and_2_out, COUNT[2]);
  J_K_Flip_Flop j_k_ff_4 (.J(and_3_out), .K(and_3_out), .clk(CLK), .Q(COUNT[3]));  // open: Qn, preset, reset
  and and_4 (and_4_out, and_3_out, COUNT[3]);
  J_K_Flip_Flop j_k_ff_5 (.J(and_4_out), .K(and_4_out), .clk(CLK), .Q(COUNT[4]));  // open: Qn, preset, reset
  and and_5 (and_5_out, and_4_out, COUNT[4]);
  J_K_Flip_Flop j_k_ff_6 (.J(and_5_out), .K(and_5_out), .clk(CLK), .Q(COUNT[5]));  // open: Qn, preset, reset
  and and_6 (and_6_out, and_5_out, COUNT[5]);
  J_K_Flip_Flop j_k_ff_7 (.J(and_6_out), .K(and_6_out), .clk(CLK), .Q(COUNT[6]));  // open: Qn, preset, reset
  and and_7 (and_7_out, and_6_out, COUNT[6]);
  J_K_Flip_Flop j_k_ff_8 (.J(and_7_out), .K(and_7_out), .Q(COUNT[7]));  // open: clk, Qn, preset, reset
endmodule
